// Logisim project T1.circ as structural Verilog: 6 circuits, main circuit main
module main (
  input  Start,
  input  X,
  output m1,
  output m0
);

  wire clock_1_out, comb_1_d0, comb_1_d1, D0Q0_q, D1Q1_q;

  Clock clock_1 (.out(clock_1_out));
  Register #(.width(1), .trigger("falling")) D0Q0 (.D(comb_1_d0), .Q(D0Q0_q), .clk(clock_1_out));  // open: en, clr
  Register #(.width(1), .trigger("falling")) D1Q1 (.D(comb_1_d1), .Q(D1Q1_q), .clk(clock_1_out));  // open: en, clr
  comb comb_1 (.Start(Start), .X(X), .Q0(D0Q0_q), .Q1(D1Q1_q), .m1(m1), .m0(m0), .d1(comb_1_d1), .d0(comb_1_d0));
endmodule

module D0 (
  input  Start,
  input  X,
  input  Q0,
  input  Q1,
  output D0
);

  wire and_1_out, and_2_out, not_1_out, not_2_out, not_3_out;

  and and_1 (and_1_out, Q1, not_1_out, X);
  not not_1 (not_1_out, Start);
  or or_1 (D0, and_1_out, and_2_out);
  and and_2 (and_2_out, Q0, not_2_out, not_3_out);
  not not_2 (not_2_out, Start);
  not not_3 (not_3_out, X);
endmodule

module D1 (
  input  Start,
  input  X,
  input  Q0,
  input  Q1,
  output D1
);

  wire and_1_out, and_2_out, not_1_out, not_2_out, not_3_out, not_4_out, not_5_out;

  and and_1 (and_1_out, Q1, not_1_out, not_2_out);
  not not_1 (not_1_out, Start);
  not not_2 (not_2_out, X);
  or or_1 (D1, and_1_out, and_2_out);
  and and_2 (and_2_out, not_3_out, not_4_out, not_5_out, X);
  not not_3 (not_3_out, Q1);
  not not_4 (not_4_out, Q0);
  not not_5 (not_5_out, Start);
endmodule

module m1 (
  input  Start,
  input  X,
  input  Q0,
  input  Q1,
  output m1
);

  wire not_1_out;

  not not_1 (not_1_out, Start);
  and and_1 (m1, not_1_out, Q0);
endmodule

module m0 (
  input  Start,
  input  X,
  input  Q0,
  input  Q1,
  output m0
);

  wire not_1_out;

  not not_1 (not_1_out, Start);
  and and_1 (m0, not_1_out, Q1);
endmodule

module comb (
  input  Start,
  input  X,
  input  Q0,
  input  Q1,
  output m1,
  output m0,
  output d1,
  output d0
);

  m1 m1_1 (.Start(Start), .X(X), .Q0(Q0), .Q1(Q1), .m1(m1));
  m0 m0_1 (.Start(Start), .X(X), .Q0(Q0), .Q1(Q1), .m0(m0));
  D0 d0_1 (.Start(Start), .X(X), .Q0(Q0), .Q1(Q1), .D0(d0));
  D1 d1_1 (.Start(Start), .X(X), .Q0(Q0), .Q1(Q1), .D1(d1));
endmodule
