// Logisim project T2.circ as structural Verilog: 3 circuits, main circuit main
module main (
  input  [9:0] m_IN,
  input  START,
  input  [5:0] e_IN,
  output [9:0] m_OUT,
  output [5:0] e_OUT,
  output READY
);

  wire clock_1_out;
  wire [5:0] shft_sum_1_exp_out;

  shft_sum shft_sum_1 (.m_IN(m_IN), .START(START), .CLOCK(clock_1_out), .exp_OUT(shft_sum_1_exp_out), .m_OUT(m_OUT));
  Clock clock_1 (.out(clock_1_out));
  Subtractor #(.width(6)) subtractor_1 (.b(shft_sum_1_exp_out), .out(e_OUT));  // open: a, bin, bout
endmodule

module m0 (
  input  [9:0] MANTISA_IN,
  output [9:0] MANTISA_OUT,
  output NORMAL
);


  assign MANTISA_OUT = MANTISA_IN;
  assign NORMAL = MANTISA_IN[9];
endmodule

module shft_sum (
  input  [9:0] m_IN,
  input  START,
  input  CLOCK,
  output [9:0] m_OUT,
  output [5:0] exp_OUT
);

  wire m0_1_normal, m0_2_normal, not_1_out, not_2_out, or_1_out;
  wire [5:0] adder_1_out, counter_1_q;
  wire [9:0] m0_1_mantisa_out, m0_2_mantisa_out, multiplexer_1_out, register_1_q, shifter_1_out;

  m0 m0_1 (.MANTISA_IN(m_IN), .NORMAL(m0_1_normal), .MANTISA_OUT(m0_1_mantisa_out));
  not not_1 (not_1_out, m0_1_normal);
  Multiplexer #(.width(10), .enable("false")) multiplexer_1 (
    .in0(m0_2_mantisa_out), .in1(m0_1_mantisa_out), .out(multiplexer_1_out), .sel(START));
  Register #(.width(10), .trigger("falling")) register_1 (
    .D(multiplexer_1_out), .en(not_2_out), .Q(register_1_q), .clk(CLOCK));  // open: clr
  Counter #(.width(6), .max('h3f), .trigger("falling")) counter_1 (
    .Q(counter_1_q), .clk(CLOCK), .clr(or_1_out));  // open: load, D, count, carry
  or or_1 (or_1_out, START, m0_1_normal);
  Shifter #(.width(10)) shifter_1 (.in(register_1_q), .\dist (4'b0001), .out(shifter_1_out));
  Adder #(.width(6)) adder_1 (.a(counter_1_q), .b(6'b000001), .out(adder_1_out));  // open: cin, cout
  m0 m0_2 (.MANTISA_IN(shifter_1_out), .NORMAL(m0_2_normal), .MANTISA_OUT(m0_2_mantisa_out));
  not not_2 (not_2_out, m0_2_normal);
  Multiplexer #(.width(10), .enable("false")) multiplexer_2 (
    .in0(m0_1_mantisa_out), .in1(m0_2_mantisa_out), .out(m_OUT), .sel(not_1_out));
  Register #(.width(6), .trigger("falling")) register_2 (
    .D(adder_1_out), .en(not_2_out), .Q(exp_OUT), .clk(CLOCK), .clr(m0_1_normal));

  // Other names for the same wires on the sheet: _1 = CLOCK
endmodule
